# Fritzing sketch hot wire (saved by Fritzing 0.9.3b)
circuit board: 10.525cm x 1.83062cm
circuit board: 5.30962cm x 7.01053cm
breadboards: 1

parts:
  Level = Pushbutton [package="[THT]"]
  R11 = Resistor [tolerance=±5% resistance=10k package=THT]
  R12 = Resistor [tolerance=±5% resistance=10k package=THT]
  Loop = Inductor [package="400 mil [THT]"]
  Rest_Position_1 = Inductor [package="400 mil [THT]"]
  main_wire = Inductor [package="400 mil [THT]"]
  Rest_Position_2 = Inductor [package="400 mil [THT]"]
  Bauteil2 = Arduino Uno (Rev3)
  SPKR1 = Loudspeaker
  R14 = Resistor [tolerance=±5% resistance=220 package=THT]
  LED_1_4 = ws2812b [package="smd 2812b"]
  LED_1_7 = ws2812b [package="smd 2812b"]
  LED_1_2 = ws2812b [package="smd 2812b"]
  LED_1_5 = ws2812b [package="smd 2812b"]
  LED_1_0 = ws2812b [package="smd 2812b"]
  LED_1_1 = ws2812b [package="smd 2812b"]
  LED_1_6 = ws2812b [package="smd 2812b"]
  LED_1_3 = ws2812b [package="smd 2812b"]
  R10 = Resistor [tolerance=±5% resistance=10k package=THT]
  J4 = male pin header, 4 pins [form="♂ (male)"]
  J1 = female pin header, 4 pins [form="♀ (female)"]

nets:
  VSS: Level.Pin_1, Level.Pin_2, R11.Pin_1, R12.Pin_1, Bauteil2.GND, SPKR1.pin1, LED_1_4.VSS, LED_1_7.VSS, LED_1_2.VSS, LED_1_5.VSS, LED_1_0.VSS, LED_1_1.VSS, LED_1_6.VSS, LED_1_3.VSS, R10.Pin_1
  N1: Level.Pin_3, Level.Pin_4, Bauteil2.D2
  N2: R11.Pin_0, Rest_Position_2.pin_1, Bauteil2.A2, J4.pin4, J1.pin4
  N3: R12.Pin_0, main_wire.pin_1, Bauteil2.A1, J4.pin3, J1.pin3
  N4: Loop.pin_0, Bauteil2.D12/MISO, J4.pin1, J1.pin1
  N5: Rest_Position_1.pin_1, Bauteil2.A0, R10.Pin_0, J4.pin2, J1.pin2
  N6: Bauteil2.D10_PWM/SS, LED_1_0.DIN
  N7: Bauteil2.D11_PWM/MOSI, R14.Pin_1
  VDD: Bauteil2.5V, LED_1_4.VDD, LED_1_7.VDD, LED_1_2.VDD, LED_1_5.VDD, LED_1_0.VDD, LED_1_1.VDD, LED_1_6.VDD, LED_1_3.VDD
  N8: SPKR1.pin2, R14.Pin_0
  N9: LED_1_4.DOUT, LED_1_5.DIN
  N10: LED_1_4.DIN, LED_1_3.DOUT
  N11: LED_1_7.DIN, LED_1_6.DOUT
  N12: LED_1_2.DOUT, LED_1_3.DIN
  N13: LED_1_2.DIN, LED_1_1.DOUT
  N14: LED_1_5.DOUT, LED_1_6.DIN
  N15: LED_1_0.DOUT, LED_1_1.DIN
